# Fritzing sketch ESP (saved by Fritzing 0.9.3b)
breadboards: 1

parts:
  R1 = Rotary Potentiometer (Large) [maximum_resistance=100kΩ package=THT]
  U3 = NodeMCU V1.0

nets:
  N1: R1.leg1, U3.3V3
  N2: R1.wiper, U3.A0
  N3: R1.leg2, U3.GND

custom parts:
  NodeMCU V1.0: ESP8266 based NodeMCU
