# Fritzing sketch SGH_ARDUINO (saved by Fritzing 0.9.3b)
breadboards: 1

parts:
  LED2 = LED - 5mm [color="Green (555nm)" package="5 mm [THT]"]
  LED3 = LED - 5mm [color="Green (555nm)" package="5 mm [THT]"]
  LED4 = LED - 5mm [color="Red (633nm)" package="5 mm [THT]"]  # not connected
  R1 = Resistor [tolerance=±5% resistance=330 package=THT]
  R2 = Resistor [tolerance=±5% resistance=330 package=THT]
  R3 = Resistor [tolerance=±5% resistance=330 package=THT]
  Componente1 = Arduino Uno (Rev3)
  Componente2 = SRF05 Ultrasonic Rangefinder
  BT1 = Bluetooth HC-06u [package=THT]
  J1 = Basic Servo
  VCC1 = Battery  # not connected

nets:
  N1: LED2.cathode, R3.Pin_1
  N2: LED2.anode, Componente1.D12/MISO
  N3: LED3.cathode, R2.Pin_1
  N4: LED3.anode, Componente1.D6_PWM
  GND: R1.Pin_0, R2.Pin_0, R3.Pin_0, Componente1.GND, Componente2.GND, BT1.GND
  N5: Componente1.D8, Componente2.Trig
  N6: Componente1.D2, BT1.TXD
  N7: Componente1.D3_PWM, BT1.RXD
  N8: Componente1.D5_PWM, J1.pulse
  N9: Componente1.D7, Componente2.Echo
  VCC: Componente1.5V, Componente2.VCC, BT1.VCC

custom parts:
  Bluetooth HC-06u: Bluetooth HC-06 - face up, pins down 16.5mm x 37.5mm PCB
